// Logisim project 4位FA.circ as structural Verilog
module \_1位FA  (
  input  X,
  input  Y,
  input  Ci,
  output F,
  output Co
);

  wire and_1_out, and_2_out, and_3_out, and_4_out, and_5_out, and_6_out, and_7_out, not_1_out, not_2_out,
       not_3_out, not_4_out, not_5_out, not_6_out;

  not not_1 (not_1_out, X);
  not not_2 (not_2_out, Y);
  not not_3 (not_3_out, X);
  not not_4 (not_4_out, Ci);
  not not_5 (not_5_out, Y);
  not not_6 (not_6_out, Ci);
  and and_1 (and_1_out, Y, Ci);
  and and_2 (and_2_out, X, Ci);
  and and_3 (and_3_out, X, Y);
  and and_4 (and_4_out, not_1_out, not_2_out, Ci);
  and and_5 (and_5_out, not_3_out, Y, not_4_out);
  and and_6 (and_6_out, X, not_5_out, not_6_out);
  and and_7 (and_7_out, X, Y, Ci);
  or or_1 (Co, and_1_out, and_2_out, and_3_out);
  or or_2 (F, and_4_out, and_5_out, and_6_out, and_7_out);
endmodule

module \_4位加法器  (
  input  in_1,
  input  in_2,
  input  in_3,
  input  in_4,
  input  in_5,
  input  in_6,
  input  in_7,
  input  in_8,
  input  in_9,
  output out_10,
  output out_11,
  output out_12,
  output out_13,
  output out_14
);

  wire \n1位fa_1_co , \n1位fa_2_co , \n1位fa_3_co ;

  \_1位FA  \u_1位fa_1  (.X(in_1), .Y(in_8), .Ci(in_9), .F(out_10), .Co(\n1位fa_1_co ));
  \_1位FA  \u_1位fa_2  (.X(in_3), .Y(in_2), .Ci(\n1位fa_1_co ), .F(out_11), .Co(\n1位fa_2_co ));
  \_1位FA  \u_1位fa_3  (.X(in_5), .Y(in_4), .Ci(\n1位fa_2_co ), .F(out_12), .Co(\n1位fa_3_co ));
  \_1位FA  \u_1位fa_4  (.X(in_7), .Y(in_6), .Ci(\n1位fa_3_co ), .F(out_13), .Co(out_14));
endmodule

module \_4位补码  (
  input  in_1,
  input  in_2,
  input  in_3,
  input  in_4,
  input  in_5,
  input  in_6,
  input  in_7,
  input  in_8,
  input  in_9,
  output out_10,
  output out_11,
  output out_12,
  output out_13,
  output out_14
);

  wire \n1位fa_1_co , \n1位fa_2_co , \n1位fa_3_co , xor_1_out, xor_2_out, xor_3_out, xor_4_out;

  xor xor_1 (xor_1_out, in_1, in_3);
  \_1位FA  \u_1位fa_1  (.X(in_2), .Y(xor_1_out), .Ci(in_1), .F(out_10), .Co(\n1位fa_1_co ));
  xor xor_2 (xor_2_out, in_1, in_5);
  \_1位FA  \u_1位fa_2  (.X(in_4), .Y(xor_2_out), .Ci(\n1位fa_1_co ), .F(out_11), .Co(\n1位fa_2_co ));
  \_1位FA  \u_1位fa_3  (.X(in_6), .Y(xor_3_out), .Ci(\n1位fa_2_co ), .F(out_12), .Co(\n1位fa_3_co ));
  xor xor_3 (xor_3_out, in_1, in_7);
  xor xor_4 (xor_4_out, in_1, in_9);
  \_1位FA  \u_1位fa_4  (.X(in_8), .Y(xor_4_out), .Ci(\n1位fa_3_co ), .F(out_13), .Co(out_14));
endmodule

module XIN (
  input  in_1,
  input  in_2,
  input  in_3,
  input  in_4,
  input  in_5,
  input  in_6,
  input  in_7,
  input  in_8,
  input  in_9,
  output out_10,
  output out_11,
  output out_12,
  output out_13,
  output \V溢出检测 ,
  output out_15
);

  wire \n1位fa_1_co , \n1位fa_2_co , \n1位fa_3_co , xor_1_out, xor_2_out, xor_3_out, xor_4_out;

  xor xor_1 (xor_1_out, in_1, in_3);
  \_1位FA  \u_1位fa_1  (.X(in_2), .Y(xor_1_out), .Ci(in_1), .F(out_10), .Co(\n1位fa_1_co ));
  xor xor_2 (xor_2_out, in_1, in_5);
  \_1位FA  \u_1位fa_2  (.X(in_4), .Y(xor_2_out), .Ci(\n1位fa_1_co ), .F(out_11), .Co(\n1位fa_2_co ));
  \_1位FA  \u_1位fa_3  (.X(in_6), .Y(xor_3_out), .Ci(\n1位fa_2_co ), .F(out_12), .Co(\n1位fa_3_co ));
  xor xor_3 (xor_3_out, in_1, in_7);
  xor xor_4 (xor_4_out, in_1, in_9);
  \_1位FA  \u_1位fa_4  (.X(in_8), .Y(xor_4_out), .Ci(\n1位fa_3_co ), .F(out_13), .Co(out_15));
  xor xor_5 (\V溢出检测 , \n1位fa_3_co , out_15);
endmodule
