// Logisim project 实验3 溢出判断（分离器）.circ as structural Verilog: 2 circuits, main circuit main
module main (
  input  in_1,
  input  [3:0] in_2,
  input  in_3,
  input  [3:0] in_4,
  input  [3:0] in_5,
  output \溢出判断 ,
  output [3:0] out_7
);

  wire adder_2_cout, adder_3_cout, xor_3_out;
  wire [3:0] adder_1_out, and_1_out, or_1_out, subtractor_1_out, xor_1_out, xor_2_out;

  Adder #(.width(4)) adder_1 (.a(in_2), .b(in_4), .out(adder_1_out), .cin(in_1));  // open: cout
  Subtractor #(.width(4)) subtractor_1 (.a(in_2), .b(in_4), .out(subtractor_1_out), .bin(in_3));  // open: bout
  assign xor_1_out = in_2 ^ in_4;  // XOR_Gate xor_1, 4 bits wide
  assign or_1_out = in_2 | in_4;  // OR_Gate or_1, 4 bits wide
  assign and_1_out = in_2 & in_4;  // AND_Gate and_1, 4 bits wide
  assign xor_2_out = in_2 ^ in_4;  // XOR_Gate xor_2, 4 bits wide
  Multiplexer #(.select(4), .width(4)) multiplexer_1 (
    .in0(adder_1_out), .in1(subtractor_1_out), .in2(or_1_out), .in6(xor_1_out), .in9(and_1_out),
    .in15(xor_2_out), .out(out_7), .sel(in_5));  // open: in3, in4, in5, in7, in8, in10, in11, in12, in13, in14, en
  Adder #(.width(3)) adder_2 (.a(in_2[2:0]), .b(in_4[2:0]), .cin(in_1), .cout(adder_2_cout));  // open: out
  Adder #(.width(1)) adder_3 (.a(in_2[3]), .b(in_4[3]), .cin(adder_2_cout), .cout(adder_3_cout));  // open: out
  xor xor_3 (xor_3_out, adder_2_cout, adder_3_cout);
  Multiplexer #(.select(4)) multiplexer_2 (
    .in0(xor_3_out), .in1(xor_3_out), .out(\溢出判断 ), .sel(in_5));  // open: in2, in3, in4, in5, in6, in7, in8, in9, in10, in11, in12, in13, in14, in15, en
endmodule

module \加法  (
  input  [3:0] in_1,
  input  [3:0] in_2,
  output out_3
);

  wire adder_1_cout, adder_2_cout;

  Adder #(.width(1)) adder_1 (.a(in_1[3]), .b(in_2[3]), .cin(adder_2_cout), .cout(adder_1_cout));  // open: out
  Adder #(.width(3)) adder_2 (.a(in_1[2:0]), .b(in_2[2:0]), .cout(adder_2_cout));  // open: out, cin
  xor xor_1 (out_3, adder_1_cout, adder_2_cout);
endmodule
