// Logisim project 实验4 位扩展32bit.circ as structural Verilog: 1 circuit, main circuit main
module main (
  input  [2:0] ADDR,
  input  [31:0] in_2,
  input  STR,
  input  SEL,
  input  LD,
  input  CLR,
  output [31:0] out_7
);

  wire clock_1_out;

  RAM #(.addrWidth(3), .bus("separate")) ram_1 (
    .addr(ADDR), .din(in_2[31:24]), .data(out_7[31:24]), .str(STR), .sel(SEL), .clk(clock_1_out), .ld(LD),
    .clr(CLR));
  RAM #(.addrWidth(3), .bus("separate")) ram_2 (
    .addr(ADDR), .din(in_2[23:16]), .data(out_7[23:16]), .str(STR), .sel(SEL), .clk(clock_1_out), .ld(LD),
    .clr(CLR));
  Clock clock_1 (.out(clock_1_out));
  RAM #(.addrWidth(3), .bus("separate")) ram_3 (
    .addr(ADDR), .din(in_2[15:8]), .data(out_7[15:8]), .str(STR), .sel(SEL), .clk(clock_1_out), .ld(LD),
    .clr(CLR));
  RAM #(.addrWidth(3), .bus("separate")) ram_4 (
    .addr(ADDR), .din(in_2[7:0]), .data(out_7[7:0]), .str(STR), .sel(SEL), .clk(clock_1_out), .ld(LD),
    .clr(CLR));
endmodule
