// Logisim project 实验4 字位扩展（思考题）.circ as structural Verilog: 1 circuit, main circuit main
module main (
  input  [7:0] \输入 ,
  input  [9:0] \地址 ,
  input  \OE可读 ,
  input  \WE可写 ,
  output [7:0] out_5
);

  wire and_1_out, and_2_out, and_3_out, and_4_out, and_5_out, and_6_out, and_7_out, and_8_out, clock_1_out,
       decoder_1_out0, decoder_1_out1, decoder_1_out2, decoder_1_out3;

  Decoder #(.select(2), .enable("false")) decoder_1 (
    .out0(decoder_1_out0), .out1(decoder_1_out1), .out2(decoder_1_out2), .out3(decoder_1_out3),
    .sel(\地址 [9:8]));
  Clock clock_1 (.out(clock_1_out));
  and and_1 (and_1_out, decoder_1_out0, \OE可读 );
  and and_2 (and_2_out, decoder_1_out1, \OE可读 );
  and and_3 (and_3_out, decoder_1_out2, \OE可读 );
  and and_4 (and_4_out, decoder_1_out3, \OE可读 );
  and and_5 (and_5_out, decoder_1_out0, \WE可写 );
  and and_6 (and_6_out, decoder_1_out1, \WE可写 );
  and and_7 (and_7_out, decoder_1_out2, \WE可写 );
  and and_8 (and_8_out, decoder_1_out3, \WE可写 );
  RAM #(.dataWidth(4), .bus("separate")) ram_1 (
    .addr(\地址 [7:0]), .din(\输入 [7:4]), .data(out_5[7:4]), .str(and_5_out), .clk(clock_1_out), .ld(and_1_out));  // open: sel, clr
  RAM #(.dataWidth(4), .bus("separate")) ram_2 (
    .addr(\地址 [7:0]), .din(\输入 [7:4]), .data(out_5[7:4]), .str(and_6_out), .clk(clock_1_out), .ld(and_2_out));  // open: sel, clr
  RAM #(.dataWidth(4), .bus("separate")) ram_3 (
    .addr(\地址 [7:0]), .din(\输入 [7:4]), .data(out_5[7:4]), .str(and_7_out), .clk(clock_1_out), .ld(and_3_out));  // open: sel, clr
  RAM #(.dataWidth(4), .bus("separate")) ram_4 (
    .addr(\地址 [7:0]), .din(\输入 [7:4]), .data(out_5[7:4]), .str(and_8_out), .clk(clock_1_out), .ld(and_4_out));  // open: sel, clr
  RAM #(.dataWidth(4), .bus("separate")) ram_5 (
    .addr(\地址 [7:0]), .din(\输入 [3:0]), .data(out_5[3:0]), .str(and_5_out), .clk(clock_1_out), .ld(and_1_out));  // open: sel, clr
  RAM #(.dataWidth(4), .bus("separate")) ram_6 (
    .addr(\地址 [7:0]), .din(\输入 [3:0]), .data(out_5[3:0]), .str(and_6_out), .clk(clock_1_out), .ld(and_2_out));  // open: sel, clr
  RAM #(.dataWidth(4), .bus("separate")) ram_7 (
    .addr(\地址 [7:0]), .din(\输入 [3:0]), .data(out_5[3:0]), .str(and_7_out), .clk(clock_1_out), .ld(and_3_out));  // open: sel, clr
  RAM #(.dataWidth(4), .bus("separate")) ram_8 (
    .addr(\地址 [7:0]), .din(\输入 [3:0]), .data(out_5[3:0]), .str(and_8_out), .clk(clock_1_out), .ld(and_4_out));  // open: sel, clr
endmodule
