// Logisim project 实验5 综合.circ as structural Verilog: 5 circuits, main circuit main
module main (
  input  DATAoe,
  input  Soe,
  input  [3:0] DATA,
  input  [1:0] \左_右移位数 ,
  input  [1:0] ST_OP,
  input  PSWce,
  input  [3:0] ALU_OP,
  input  CF,
  input  [1:0] INDEX,
  input  GRSoe,
  input  Ace,
  input  GRSce,
  input  RESET
);

  wire alu_1_cf_2, alu_1_of, alu_1_sf, alu_1_zf, CLK_out, psw_1_cf, psw_1_of, psw_1_sf, psw_1_zf;
  wire [3:0] alu_1_f, controlled_buffer_1_out, controlled_buffer_2_out, controlled_buffer_4_out, \grs_1_输出 ,
       \shifter_1_输出 , \暂存器_q ;

  assign controlled_buffer_1_out = GRSce ? controlled_buffer_2_out : 4'bz;  // Controlled_Buffer controlled_buffer_1
  LED OF (.in(psw_1_of));
  LED u_CF (.in(psw_1_cf));
  PSW psw_1 (
    .PSWce(PSWce), .in_2(alu_1_of), .in_3(alu_1_cf_2), .in_4(alu_1_sf), .in_5(alu_1_zf), .RESET(RESET),
    .OF(psw_1_of), .CF(psw_1_cf), .SF(psw_1_sf), .ZF(psw_1_zf));
  GRS grs_1 (.\输入 (controlled_buffer_1_out), .INDEX(INDEX), .CLK(CLK_out), .\输出 (\grs_1_输出 ));  // open: RESET
  assign controlled_buffer_2_out = GRSoe ? \grs_1_输出  : 4'bz;  // Controlled_Buffer controlled_buffer_2
  assign controlled_buffer_2_out = DATAoe ? DATA : 4'bz;  // Controlled_Buffer controlled_buffer_3
  LED SF (.in(psw_1_sf));
  LED ZF (.in(psw_1_zf));
  Hex_Digit_Display hex_digit_display_1 (.value(\grs_1_输出 ));  // open: dp
  Hex_Digit_Display hex_digit_display_2 (.value(\暂存器_q ));  // open: dp
  assign controlled_buffer_4_out = Ace ? controlled_buffer_2_out : 4'bz;  // Controlled_Buffer controlled_buffer_4
  Register #(.width(4)) \u_暂存器  (.D(controlled_buffer_4_out), .Q(\暂存器_q ), .clk(CLK_out), .clr(RESET));  // open: en
  // Probe on controlled_buffer_2_out
  assign controlled_buffer_2_out = Soe ? \shifter_1_输出  : 4'bz;  // Controlled_Buffer controlled_buffer_5
  Hex_Digit_Display hex_digit_display_3 (.value(\shifter_1_输出 ));  // open: dp
  ALU alu_1 (
    .dst(\暂存器_q ), .src(controlled_buffer_2_out), .CF(CF), .ALU_OP(ALU_OP), .OF(alu_1_of), .CF_2(alu_1_cf_2),
    .SF(alu_1_sf), .ZF(alu_1_zf), .F(alu_1_f));
  SHIFTER shifter_1 (
    .ST_OP(ST_OP), .F(alu_1_f), .\左_右移位数 (\左_右移位数 ), .\输出 (\shifter_1_输出 ), .RESET(RESET), .CLK(CLK_out));
  Hex_Digit_Display hex_digit_display_4 (.value(alu_1_f));  // open: dp
  // Probe on alu_1_f
  Hex_Digit_Display hex_digit_display_5 (.value(controlled_buffer_2_out));  // open: dp
  // Probe on controlled_buffer_2_out
  Clock CLK (.out(CLK_out));
endmodule

module SHIFTER (
  input  RESET,
  input  CLK,
  input  [1:0] ST_OP,
  input  [1:0] \左_右移位数 ,
  input  [3:0] F,
  output [3:0] \输出 
);

  wire decoder_1_out1, decoder_1_out2, decoder_1_out3;
  wire [3:0] controlled_buffer_1_out, shifter_1_out, shifter_2_out;

  Decoder #(.select(2), .enable("false")) decoder_1 (
    .out1(decoder_1_out1), .out2(decoder_1_out2), .out3(decoder_1_out3), .sel(ST_OP));  // open: out0
  assign controlled_buffer_1_out = decoder_1_out1 ? shifter_1_out : 4'bz;  // Controlled_Buffer controlled_buffer_1
  Shifter #(.width(4), .shift("lr")) shifter_1 (.in(F), .\dist (\左_右移位数 ), .out(shifter_1_out));
  Shifter #(.width(4)) shifter_2 (.in(F), .\dist (\左_右移位数 ), .out(shifter_2_out));
  assign controlled_buffer_1_out = decoder_1_out2 ? shifter_2_out : 4'bz;  // Controlled_Buffer controlled_buffer_2
  Register #(.width(4)) register_1 (.D(controlled_buffer_1_out), .Q(\输出 ), .clk(CLK), .clr(RESET));  // open: en
  assign controlled_buffer_1_out = decoder_1_out3 ? F : 4'bz;  // Controlled_Buffer controlled_buffer_3
endmodule

// ALU+PSW
module ALU (
  input  [3:0] dst,
  input  [3:0] src,
  input  CF,
  input  [3:0] ALU_OP,
  output OF,
  output CF_2,
  output SF,
  output ZF,
  output [3:0] F
);

  wire adder_4_cout, adder_5_cout, xor_2_out;
  wire [3:0] adder_1_out, adder_2_out, adder_3_out, and_1_out, not_1_out, or_1_out, subtractor_1_out,
       subtractor_2_out, subtractor_3_out, xor_1_out;

  Adder #(.width(4)) adder_1 (.a(dst), .b(src), .out(adder_1_out), .cout(CF_2));  // open: cin
  Adder #(.width(4)) adder_2 (.a(dst), .b(src), .out(adder_2_out), .cin(CF), .cout(CF_2));
  Subtractor #(.width(4)) subtractor_1 (.a(dst), .b(src), .out(subtractor_1_out));  // open: bin, bout
  Subtractor #(.width(4)) subtractor_2 (.a(dst), .b(src), .out(subtractor_2_out), .bin(CF));  // open: bout
  assign and_1_out = dst & src;  // AND_Gate and_1, 4 bits wide
  assign or_1_out = dst | src;  // OR_Gate or_1, 4 bits wide
  assign not_1_out = ~dst;  // NOT_Gate not_1, 4 bits wide
  assign xor_1_out = dst ^ src;  // XOR_Gate xor_1, 4 bits wide
  Adder #(.width(4)) adder_3 (.a(dst), .b(4'b0001), .out(adder_3_out));  // open: cin, cout
  Subtractor #(.width(4)) subtractor_3 (.a(dst), .b(4'b0001), .out(subtractor_3_out));  // open: bin, bout
  Adder #(.width(3)) adder_4 (.a(src[2:0]), .b(dst[2:0]), .cout(adder_4_cout));  // open: out, cin
  Adder #(.width(1)) adder_5 (.a(src[3]), .b(dst[3]), .cin(adder_4_cout), .cout(adder_5_cout));  // open: out
  xor xor_2 (xor_2_out, adder_4_cout, adder_5_cout);
  Multiplexer #(.select(4), .width(4), .enable("false")) multiplexer_1 (
    .in0(dst), .in1(adder_1_out), .in2(adder_2_out), .in3(subtractor_1_out), .in4(subtractor_2_out),
    .in5(and_1_out), .in6(or_1_out), .in7(not_1_out), .in8(xor_1_out), .in9(adder_3_out),
    .in10(subtractor_3_out), .out(F), .sel(ALU_OP));  // open: in11, in12, in13, in14, in15
  Multiplexer #(.select(3), .enable("false")) multiplexer_2 (
    .in1(xor_2_out), .in2(xor_2_out), .in3(xor_2_out), .in4(xor_2_out), .out(OF), .sel(ALU_OP[2:0]));  // open: in0, in5, in6, in7
  Comparator #(.width(4)) comparator_1 (.a(4'b0000), .b(F), .eq(ZF));  // open: gt, lt

  assign SF = F[3];
endmodule

module GRS (
  input  [3:0] \输入 ,
  input  [1:0] INDEX,
  input  CLK,
  input  RESET,
  output [3:0] \输出 
);

  wire decoder_1_out0, decoder_1_out1, decoder_1_out2, decoder_1_out3;
  wire [3:0] register_1_q, register_2_q, register_3_q, register_4_q;

  Decoder #(.select(2), .enable("false")) decoder_1 (
    .out0(decoder_1_out0), .out1(decoder_1_out1), .out2(decoder_1_out2), .out3(decoder_1_out3), .sel(INDEX));
  Register #(.width(4)) register_1 (.D(\输入 ), .en(decoder_1_out0), .Q(register_1_q), .clk(CLK), .clr(RESET));
  Register #(.width(4)) register_2 (.D(\输入 ), .en(decoder_1_out1), .Q(register_2_q), .clk(CLK), .clr(RESET));
  Register #(.width(4)) register_3 (.D(\输入 ), .en(decoder_1_out2), .Q(register_3_q), .clk(CLK), .clr(RESET));
  Register #(.width(4)) register_4 (.D(\输入 ), .en(decoder_1_out3), .Q(register_4_q), .clk(CLK), .clr(RESET));
  Multiplexer #(.select(2), .width(4), .enable("false")) multiplexer_1 (
    .in0(register_1_q), .in1(register_2_q), .in2(register_3_q), .in3(register_4_q), .out(\输出 ), .sel(INDEX));
endmodule

module PSW (
  input  PSWce,
  input  in_2,
  input  in_3,
  input  in_4,
  input  in_5,
  input  RESET,
  output OF,
  output CF,
  output SF,
  output ZF
);

  wire [3:0] controlled_buffer_1_out, xor_1_out;

  assign controlled_buffer_1_out = PSWce ? {in_2, in_3, in_4, in_5} : 4'bz;  // Controlled_Buffer controlled_buffer_1
  assign xor_1_out = {in_2, in_3, in_4, in_5} ^ {in_2, in_3, in_4, in_5};  // XOR_Gate xor_1, 4 bits wide
  Multiplexer #(.width(4), .enable("false")) multiplexer_1 (
    .in0(controlled_buffer_1_out), .in1(xor_1_out), .out({OF, CF, SF, ZF}), .sel(RESET));
endmodule
